# Fritzing sketch Leiterplatte_Luftschiff (saved by Fritzing 0.9.2b)
circuit board: 8.67078cm x 6.98249cm
breadboards: 1

parts:
  Bauteil1 = Arduino Micro (Rev3)
  Treiber_Vortrieb = L293D [package=THT]
  Treiber_Höhe = L293D [package=THT]
  VCC1 = Battery block 9V

nets:
  N1: Bauteil1.D5_PWM, Treiber_Vortrieb.In_2
  N2: Bauteil1.D6_PWM/A7, Treiber_Vortrieb.In_1
  N3: Bauteil1.D9_PWM/A9, Treiber_Vortrieb.In_3
  N4: Bauteil1.D10_PWM/A10, Treiber_Vortrieb.In_4
  N5: Bauteil1.D11_PWM, Treiber_Höhe.In_1
  N6: Bauteil1.D12_PWM/A11, Treiber_Vortrieb.Enable_1, Treiber_Vortrieb.Enable_2, Treiber_Höhe.Enable_1
  N7: Bauteil1.GND, Treiber_Vortrieb.0V, Treiber_Höhe.0V, VCC1.-
  N8: Bauteil1.5V, Treiber_Vortrieb.+V
  N9: Bauteil1.D13_PWM, Treiber_Höhe.In_2
  N10: Treiber_Vortrieb.+Vmotor, Treiber_Höhe.+Vmotor, VCC1.+
